// Digital circuit part_c.dig as structural Verilog
module part_c (
  input  in_2,
  input  in_0,
  input  in_1,
  output out_0
);

  wire n0_s, n1_s, n5_d, p0_d, p3_d, p4_d, p5_d;

  PFET p0 (.G(in_0), .S(1'b1), .D(p0_d));
  PFET p1 (.G(in_1), .S(1'b1), .D(p0_d));
  NFET n0 (.G(in_0), .D(p0_d), .S(n0_s));
  NFET n1 (.G(in_1), .D(n0_s), .S(n1_s));
  NFET n2 (.G(in_2), .D(n1_s), .S(1'b0));
  PFET p2 (.G(in_2), .S(1'b1), .D(p0_d));
  PFET p3 (.G(in_2), .S(1'b1), .D(p3_d));
  NFET n3 (.G(in_2), .D(p3_d), .S(1'b0));
  PFET p4 (.G(p0_d), .S(1'b1), .D(p4_d));
  NFET n4 (.G(p0_d), .D(p4_d), .S(1'b0));
  NFET n5 (.G(p3_d), .D(n5_d), .S(1'b0));
  PFET p5 (.G(p4_d), .S(1'b1), .D(p5_d));
  PFET p6 (.G(p3_d), .S(p5_d), .D(n5_d));
  NFET n6 (.G(p4_d), .D(n5_d), .S(1'b0));
  PFET p7 (.G(n5_d), .S(1'b1), .D(out_0));
  NFET n7 (.G(n5_d), .D(out_0), .S(1'b0));
endmodule

/* Test case part_c_test:
in_0 in_1 in_2 out_0
  0    0    0    1
  0    0    1    0
  0    1    0    1
  0    1    1    0
  1    0    0    1
  1    0    1    0
  1    1    0    1
  1    1    1    1
*/
